// Digital circuit gaming pc.dig as structural Verilog
module gaming_pc (
  input  clk
);

  wire Address_High_Read, Address_Low_Read, ALU_Enable, and_1_out, and_2_out, and_3_out, and_4_out,
       and_5_out, and_6_out, BP_Direction, BP_Enable, BP_Write, Carry, Carry_Flag_q, Carry_Write, Cin_Select,
       Clock, Comparator_Select, Cond__Flag_q, Condition_Enable, Condition_Invert, Condition_Out,
       Condition_Write, d_ff_1_nq, gaming_alu_1_a_eq_b, gaming_alu_1_cout, IO_Read, IO_Write, IP_Conditional,
       IP_Direction, IP_Enable, IP_Write, M, Memory_Load, Memory_Ready, Memory_Store, multiplexer_2_out,
       multiplexer_3_out, Next_Instruction, None, not_1_out, not_2_out, not_3_out, or_1_out, or_2_out,
       or_3_out, Reg_A_Read, Reg_A_Write, Reg_B_Read, Reg_B_Write, S0, S1, S2, S3, SP_Direction, SP_Enable,
       SP_Write, xor_1_out, xor_2_out;
  wire [1:0] Address_Select;
  wire [2:0] Bus_Select;
  wire [4:0] Stage_Counter_out;
  wire [7:0] A, B, driver_1_out, gaming_alu_1_out, Instruction_q;
  wire [15:0] BP, IP_out, multiplexer_1_out, Stack_Pointer_out;
  wire [31:0] counter_1_out;

  D_FF d_ff_1 (.D(1'b1), .C(Clock), .nQ(d_ff_1_nq));  // open: Q
  or or_1 (or_1_out, d_ff_1_nq, SP_Enable);
  or or_2 (or_2_out, IP_Enable, Condition_Out);
  and and_1 (and_1_out, or_3_out, Next_Instruction);
  or or_3 (or_3_out, and_2_out, not_1_out);
  and and_2 (and_2_out, Condition_Out, Condition_Enable);
  Register #(.Bits(8)) Register_A (.D(driver_1_out), .C(Clock), .en(Reg_A_Write), .Q(A));
  Register #(.Bits(8)) Register_B (.D(driver_1_out), .C(Clock), .en(Reg_B_Write), .Q(B));
  CounterPreset #(.Bits(16)) Base_Pointer (
    .en(BP_Enable), .C(Clock), .dir(BP_Direction), .in(multiplexer_1_out), .ld(BP_Write), .clr(1'b0), .out(BP));  // open: ovf
  CounterPreset #(.Bits(16)) Stack_Pointer (
    .en(or_1_out), .C(Clock), .dir(~SP_Direction), .in(multiplexer_1_out), .ld(SP_Write), .clr(1'b0),
    .out(Stack_Pointer_out));  // open: ovf
  CounterPreset #(.Bits(16)) IP (
    .en(or_2_out), .C(Clock), .dir(IP_Direction), .in(multiplexer_1_out), .ld(IP_Write), .clr(1'b0),
    .out(IP_out));  // open: ovf
  Register #(.Bits(8)) Instruction (.D(driver_1_out), .C(Clock), .en(and_1_out), .Q(Instruction_q));
  Counter #(.Bits(5)) Stage_Counter (.en(1'b1), .C(Clock), .clr(and_1_out), .out(Stage_Counter_out));  // open: ovf
  not not_1 (not_1_out, Condition_Enable);
  Counter #(.Bits(32)) counter_1 (.en(1'b1), .C(Clock), .clr(1'b0), .out(counter_1_out));  // open: ovf
  // Probe SP on Stack_Pointer_out
  // Probe IP on IP_out
  // Probe Instruction on Instruction_q
  // Probe Stage on Stage_Counter_out
  // Probe Total Cycles on counter_1_out
  assign driver_1_out = Reg_B_Read ? B : 8'bz;  // Driver driver_1
  Multiplexer #(.Selector_Bits(2), .Bits(16)) multiplexer_1 (
    .sel(Address_Select), .in_0({A, B}), .in_1(BP), .in_2(Stack_Pointer_out), .in_3(IP_out),
    .out(multiplexer_1_out));
  ROM #(.AddrBits(13), .Bits(32)) Control_ROM (
    .A({Instruction_q, Stage_Counter_out}), .sel(1'b1),
    .D({IO_Write, Condition_Enable, Condition_Write, Condition_Invert, Comparator_Select, Carry_Write, Cin_Select, IP_Direction, Carry, M, S3, S2, S1, S0, Next_Instruction, IP_Enable, IP_Write, IP_Conditional, SP_Enable, SP_Direction, SP_Write, BP_Enable, BP_Direction, BP_Write, Reg_B_Write, Reg_A_Write, Memory_Store, Bus_Select, Address_Select}));
  assign driver_1_out = Address_Low_Read ? multiplexer_1_out[7:0] : 8'bz;  // Driver driver_2
  assign driver_1_out = Address_High_Read ? multiplexer_1_out[15:8] : 8'bz;  // Driver driver_3
  // Probe Address on multiplexer_1_out
  // Probe BP on BP
  // Probe Bus on driver_1_out
  assign driver_1_out = Reg_A_Read ? A : 8'bz;  // Driver driver_4
  // Probe A on A
  // Probe B on B
  gaming_ram gaming_ram_1 (
    .A(multiplexer_1_out), .ld(Memory_Load), .str(Memory_Store), .C(Clock), .D(driver_1_out), .r(Memory_Ready));
  Demultiplexer #(.Selector_Bits(3)) demultiplexer_1 (
    .sel(Bus_Select), .in(1'b1), .out_0(Memory_Load), .out_1(ALU_Enable), .out_2(Reg_A_Read),
    .out_3(Reg_B_Read), .out_4(Address_Low_Read), .out_5(Address_High_Read), .out_6(IO_Read), .out_7(None));
  gaming_externals gaming_externals_1 (.Bus(driver_1_out), .Read(IO_Read), .Write(IO_Write), .Clock(Clock));
  and and_3 (and_3_out, Clock, Carry_Write);
  Multiplexer multiplexer_2 (.sel(Cin_Select), .in_0(Carry_Flag_q), .in_1(Carry), .out(multiplexer_2_out));
  not not_2 (not_2_out, Memory_Load);
  not not_3 (not_3_out, Memory_Store);
  D_FF Carry_Flag (.D(gaming_alu_1_cout), .C(and_3_out), .Q(Carry_Flag_q));  // open: nQ
  gaming_alu gaming_alu_1 (
    .A(A), .B(B), .S({S3, S2, S1, S0}), .M(M), .Cin(multiplexer_2_out), .CF(xor_2_out),
    .Out(gaming_alu_1_out), .Cout(gaming_alu_1_cout), .A_eq_B(gaming_alu_1_a_eq_b));
  and and_4 (and_4_out, Memory_Ready, clk);
  and and_5 (and_5_out, clk, not_2_out, not_3_out);
  assign driver_1_out = ALU_Enable ? gaming_alu_1_out : 8'bz;  // Driver driver_5
  or or_4 (Clock, and_4_out, and_5_out);
  xor xor_1 (xor_1_out, Condition_Invert, multiplexer_3_out);
  Multiplexer multiplexer_3 (
    .sel(Comparator_Select), .in_0(gaming_alu_1_cout), .in_1(gaming_alu_1_a_eq_b), .out(multiplexer_3_out));
  and and_6 (and_6_out, Clock, Condition_Write);
  D_FF Cond__Flag (.D(xor_1_out), .C(and_6_out), .Q(Cond__Flag_q));  // open: nQ
  xor xor_2 (xor_2_out, Condition_Invert, Cond__Flag_q);
  and and_7 (Condition_Out, xor_2_out, Condition_Enable);

  // Notes on the sheet:
  //   clk: Hz: 10
  //   contents of Control_ROM (hex, n*v repeats v):
  //   30003,0,0,0,0,0,0,0,0,0,0,0,0,0,0,0,0,0,0,0,0,0,0,0,0,0,0,0,0,0,0,0,12043,1a,30003,
  //   0,0,0,0,0,0,0,0,0,0,0,0,0,0,0,0,0,0,0,0,0,0,0,0,0,0,0,0,0,12043,10083,202e,2a,30003,
  //   0,0,0,0,0,0,0,0,0,0,0,0,0,0,0,0,0,0,0,0,0,0,0,0,0,0,0,33003,0,0,0,0,0,0,0,0,0,0,0,
  //   0,0,0,0,0,0,0,0,0,0,0,0,0,0,0,0,0,0,0,0,301c,33003,0,0,0,0,0,0,0,0,0,0,0,0,0,0,0,
  //   0,0,0,0,0,0,0,0,0,0,0,0,0,0,0,52,10083,6a40084,56,44,281c,30003,0,0,0,0,0,0,0,0,0,
  //   0,0,0,0,0,0,0,0,0,0,0,0,0,0,0,0,2042,2a,30003,0,0,0,0,0,0,0,0,0,0,0,0,0,0,0,0,0,0,
  //   0,0,0,0,0,0,0,0,0,0,0,0,0,0,0,0,0,0,0,0,0,0,0,0,0,0,0,0,0,0,0,0,0,0,0,0,0,0,0,0,0,
  //   0,0,0,0,0,0,0,0,0,0,0,0,0,0,0,0,0,0,0,0,0,0,0,0,0,0,0,0,0,0,0,0,0,0,0,0,0,0,0,0,0,
  //   0,0,0,0,0,0,0,0,0,0,0,0,0,0,0,0,0,0,0,0,0,0,0,0,0,0,0,0,0,0,0,0,0,0,0,0,0,0,0,0,0,
  //   0,0,0,0,0,0,0,0,0,0,0,0,0,0,0,0,3042,2082,201c,202e,2a,30003,0,0,0,0,0,0,0,0,0,0,
  //   0,0,0,0,0,0,0,0,0,0,0,0,0,0,0,0,0,0,0,0,0,0,0,0,0,0,0,0,0,0,0,0,0,0,0,0,0,0,0,0,0,
  //   0,0,0,0,0,0,0,0,0,0,0,0,0,0,0,0,0,0,0,0,0,0,0,0,0,0,0,0,0,0,0,0,0,0,0,0,0,0,0,0,0,
  //   0,0,0,0,0,0,0,0,0,0,0,0,0,0,0,0,0,0,0,0,0,0,0,0,0,0,0,0,0,0,0,0,0,0,0,0,0,0,0,0,0,
  //   0,0,0,0,0,0,0,0,0,0,0,0,0,0,0,0,0,0,0,0,0,0,0,0,0,0,0,0,0,0,0,0,0,0,0,0,0,0,0,0,0,
  //   0,0,0,0,0,0,0,0,0,0,0,0,3042,82,202a,2e,30003,0,0,0,0,0,0,0,0,0,0,0,0,0,0,0,0,0,0,
  //   0,0,0,0,0,0,0,0,0,0,0,0,0,0,0,0,0,0,0,0,0,0,0,0,0,0,0,0,0,0,0,0,0,0,0,0,0,0,0,0,0,
  //   0,0,0,0,0,0,0,0,0,0,0,0,0,0,0,0,0,0,0,0,0,0,0,0,0,0,0,0,0,0,0,0,0,0,0,0,0,0,0,0,0,
  //   0,0,0,0,0,0,0,0,0,0,0,0,0,0,0,0,0,0,0,0,0,0,0,0,0,0,0,0,0,0,0,0,0,0,0,0,0,0,0,0,0,
  //   0,0,0,0,0,0,0,0,0,0,0,0,0,0,0,0,0,0,0,0,0,0,0,0,0,0,0,0,0,0,0,0,0,0,0,0,0,0,0,0,0,
  //   0,0,0,0,0,0,0,0,0,0,0,0,0,0,0,0,0,0,0,0,0,0,0,0,0,0,0,0,0,0,0,0,0,0,0,0,0,0,0,0,0,
  //   0,0,0,0,0,0,0,0,0,0,0,0,0,0,0,0,0,0,0,0,0,0,0,0,0,0,0,0,0,0,0,0,0,0,0,0,0,0,0,0,0,
  //   0,0,0,0,0,0,0,0,0,0,0,0,0,0,0,0,0,0,0,0,0,0,0,0,0,0,0,0,0,0,0,0,0,0,0,0,0,0,0,0,0,
  //   0,0,0,0,0,0,0,0,0,0,0,0,0,0,0,0,0,0,0,0,0,0,0,0,0,0,0,0,0,0,0,0,0,0,0,0,0,0,0,0,0,
  //   0,0,0,0,0,0,0,0,0,0,0,0,0,0,0,0,0,0,0,0,0,0,0,0,0,0,0,0,0,0,0,0,0,0,0,0,0,0,0,0,0,
  //   0,0,0,0,0,0,0,0,0,0,0,0,0,0,0,0,0,0,0,0,0,0,0,0,0,0,0,0,0,0,0,0,0,0,0,0,0,0,0,0,0,
  //   0,0,0,0,0,0,0,0,0,0,0,0,0,0,0,0,0,0,0,0,0,0,0,0,0,0,0,0,0,0,0,0,0,0,0,0,0,0,0,0,0,
  //   0,0,0,0,0,0,10083,10043,2040,2a,30003,0,0,0,0,0,0,0,0,0,0,0,0,0,0,0,0,0,0,0,0,0,0,
  //   0,0,0,0,0,0,0,0,0,0,0,0,0,0,0,0,0,0,0,0,0,0,0,0,0,0,0,0,0,0,0,0,0,0,0,0,0,3082,42,
  //   40,2a,30003,0,0,0,0,0,0,0,0,0,0,0,0,0,0,0,0,0,0,0,0,0,0,0,0,0,0,0,0,0,0,0,0,0,0,0,
  //   0,0,0,0,0,0,0,0,0,0,0,0,0,0,0,0,0,0,0,0,0,0,0,0,3042,82,282024,6a43026,3082,2042,
  //   242064,3082,3040,2a,30003,0,0,0,0,0,0,0,0,0,0,0,0,0,0,0,0,0,0,0,0,0,0,0,0,0,0,0,0,
  //   0,0,0,0,0,0,0,0,0,0,0,0,0,0,0,0,0,0,0,0,0,0,0,0,0,2042,7b10083,283026,6a42026,3082,
  //   10043,240044,82,40,2a,30003,0,0,0,0,0,0,0,0,0,0,0,0,0,0,0,0,0,0,0,0,0,0,0,0,0,0,0,
  //   0,0,0,0,0,0,0,0,0,0,0,0,0,0,0,0,0,0,0,0,0,0,0,0,0,0,0,0,0,0,0,0,0,0,0,0,0,0,0,0,0,
  //   0,0,0,0,0,0,0,0,0,0,0,0,0,0,0,0,0,0,0,0,0,0,0,0,0,0,0,0,0,0,0,0,0,0,0,0,0,0,0,0,0,
  //   0,0,0,0,0,0,0,0,0,0,0,0,0,0,0,0,0,0,0,0,0,0,0,0,0,0,0,0,0,0,0,0,0,0,0,0,0,0,0,0,0,
  //   0,0,0,0,0,0,0,0,0,0,0,0,0,0,0,0,0,0,0,0,0,0,0,0,0,0,0,0,0,0,0,0,0,0,0,0,0,0,0,0,0,
  //   0,0,0,0,0,0,0,0,0,0,0,0,0,0,0,0,0,0,0,0,0,0,0,0,0,0,0,0,0,0,0,0,0,0,0,0,0,0,0,0,0,
  //   0,0,0,0,0,0,0,0,0,0,0,0,0,0,0,0,0,0,0,0,0,0,0,0,0,0,0,0,0,0,0,0,0,0,0,0,0,0,0,0,0,
  //   0,0,0,0,0,0,0,0,0,0,0,0,0,0,0,0,0,0,0,0,0,0,0,0,0,0,0,0,0,0,0,0,0,0,0,0,0,0,0,0,0,
  //   0,0,0,0,0,0,0,0,0,0,0,0,0,0,0,0,0,0,0,0,0,0,0,0,0,0,0,0,0,0,0,0,0,0,0,0,0,0,0,0,0,
  //   0,0,0,0,0,0,0,0,0,0,0,0,0,0,0,0,0,0,10083,10043,51c,42,3029,30003,0,0,0,0,0,0,0,0,
  //   0,0,0,0,0,0,0,0,0,0,0,0,0,0,0,0,0,0,2055,2a,2051,2a,13083,13043,51c,2042,2029,3082,
  //   3042,351c,30003,0,0,0,0,0,0,0,0,0,0,0,0,0,0,0,0,0,0,0,0,0,0,0,0,0,0,0,0,0,0,0,0,0,
  //   0,0,0,0,0,0,0,0,0,0,0,0,0,0,0,0,0,0,0,0,0,0,0,0,0,0,0,0,0,0,0,0,0,0,0,0,0,0,0,0,0,
  //   0,0,0,0,0,0,0,0,0,0,0,0,0,0,0,0,0,0,0,0,0,0,0,0,0,0,0,0,0,0,0,0,0,0,0,0,0,0,0,0,0,
  //   0,0,0,0,0,0,0,0,0,0,0,0,0,0,0,0,0,0,0,0,0,0,0,0,0,0,0,0,0,0,0,0,0,0,0,0,0,0,0,0,0,
  //   0,0,0,0,0,0,0,0,0,0,0,0,0,0,0,0,0,0,0,0,0,0,0,0,0,0,0,0,0,0,0,0,0,0,0,0,0,0,0,0,0,
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  //   IP Direction is placed wierdly because it would be
  //   a pain to move signals around and it would mess
  //   with a bit of nice alignment
endmodule
