// Digital circuit gaming pc.dig as structural Verilog
module gaming_pc (
  input  clk
);

  wire ALU_Enable, and_1_out, and_2_out, and_3_out, and_4_out, and_5_out, BP_Enable, BP_Write, Carry,
       Carry_Flag_q, Carry_Write, Comparator_Invert, Comparator_Select, Condition_Enable, Condition_Flag_q,
       Condition_Out, Condition_Write, gaming_alu_1_a_eq_b, gaming_alu_1_cout, IP_Conditional, IP_Enable,
       IP_Write, M, Memory_Load, Memory_Store, multiplexer_2_out, multiplexer_3_out, Next_Instruction,
       not_1_out, or_1_out, or_2_out, Reg_A_Read, Reg_A_Write, Reg_B_Read, Reg_B_Write, S0, S1, S2, S3,
       SP_Direction, SP_Enable, xor_1_out;
  wire [1:0] Address_Select;
  wire [3:0] Stage_Counter_out;
  wire [7:0] _32kx8_RAM_d, driver_1_out, driver_2_out, gaming_alu_1_out, Instruction_q, Register_A_q,
       Register_B_q;
  wire [15:0] Base_Pointer_out, IP_out, multiplexer_1_out, Stack_Pointer_out;
  wire [31:28] Control_ROM_d;

  or or_1 (or_1_out, IP_Write, Condition_Out);
  Register #(.Bits(8)) Register_A (.D(_32kx8_RAM_d), .C(clk), .en(Reg_A_Write), .Q(Register_A_q));
  Register #(.Bits(8)) Register_B (.D(_32kx8_RAM_d), .C(clk), .en(Reg_B_Write), .Q(Register_B_q));
  CounterPreset #(.Bits(16)) Base_Pointer (
    .en(BP_Enable), .C(clk), .dir(1'b0), .in(multiplexer_1_out), .ld(BP_Write), .clr(1'b0),
    .out(Base_Pointer_out));  // open: ovf
  CounterPreset #(.Bits(16)) Stack_Pointer (
    .en(SP_Enable), .C(clk), .dir(SP_Direction), .in(multiplexer_1_out), .ld(1'b0), .clr(1'b0),
    .out(Stack_Pointer_out));  // open: ovf
  CounterPreset #(.Bits(16)) IP (
    .en(IP_Enable), .C(clk), .dir(1'b0), .in(multiplexer_1_out), .ld(or_1_out), .clr(1'b0), .out(IP_out));  // open: ovf
  Register #(.Bits(8)) Instruction (.D(_32kx8_RAM_d), .C(clk), .en(Next_Instruction), .Q(Instruction_q));
  Counter #(.Bits(4)) Stage_Counter (.en(1'b1), .C(clk), .clr(Next_Instruction), .out(Stage_Counter_out));  // open: ovf
  // Probe Instruction on Instruction_q
  // Probe Stage on Stage_Counter_out
  assign driver_1_out = Reg_A_Read ? Register_A_q : 8'bz;  // Driver driver_1
  assign driver_2_out = Reg_B_Read ? Register_B_q : 8'bz;  // Driver driver_2
  Multiplexer #(.Selector_Bits(2), .Bits(16)) multiplexer_1 (
    .sel(Address_Select), .in_0({Register_B_q, Register_A_q}), .in_1(Base_Pointer_out),
    .in_2(Stack_Pointer_out), .in_3(IP_out), .out(multiplexer_1_out));
  ROM #(.AddrBits(12), .isProgramMemory("true"), .Bits(32)) Control_ROM (
    .A({Instruction_q, Stage_Counter_out}), .sel(1'b1),
    .D({Control_ROM_d, Condition_Write, Condition_Enable, Comparator_Invert, Comparator_Select, ALU_Enable, Carry_Write, Carry, M, S3, S2, S1, S0, Next_Instruction, IP_Enable, IP_Write, IP_Conditional, SP_Direction, SP_Enable, BP_Enable, BP_Write, Reg_B_Read, Reg_B_Write, Reg_A_Read, Reg_A_Write, Memory_Store, Memory_Load, Address_Select}));
  // Probe Address on multiplexer_1_out
  // Probe Bus on _32kx8_RAM_d
  and and_1 (and_1_out, multiplexer_1_out[15], Memory_Store);
  and and_2 (and_2_out, multiplexer_1_out[15], Memory_Load);
  not not_1 (not_1_out, multiplexer_1_out[15]);
  and and_3 (and_3_out, not_1_out, Memory_Load);
  RAMSinglePort #(.AddrBits(15), .Bits(8)) _32kx8_RAM (
    .A(multiplexer_1_out[14:0]), .str(and_1_out), .C(clk), .ld(and_2_out), .D(_32kx8_RAM_d));
  ROM #(.AddrBits(15), .Bits(8)) _32kx8_ROM (.A(multiplexer_1_out[14:0]), .sel(and_3_out), .D(_32kx8_RAM_d));
  or or_2 (or_2_out, Carry_Write, ALU_Enable);
  and and_4 (and_4_out, clk, or_2_out);
  gaming_alu gaming_alu_1 (
    .A(driver_1_out), .B(driver_2_out), .S({S3, S2, S1, S0}), .M(M), .Cin(Carry_Flag_q),
    .Out(gaming_alu_1_out), .Cout(gaming_alu_1_cout), .A_eq_B(gaming_alu_1_a_eq_b));
  D_FF Carry_Flag (.D(multiplexer_3_out), .C(and_4_out), .Q(Carry_Flag_q));  // open: nQ
  Multiplexer multiplexer_2 (
    .sel(Comparator_Select), .in_0(gaming_alu_1_cout), .in_1(gaming_alu_1_a_eq_b), .out(multiplexer_2_out));
  assign _32kx8_RAM_d = ALU_Enable ? gaming_alu_1_out : 8'bz;  // Driver driver_3
  Multiplexer multiplexer_3 (.sel(Carry_Write), .in_0(gaming_alu_1_cout), .in_1(Carry), .out(multiplexer_3_out));
  xor xor_1 (xor_1_out, multiplexer_2_out, Comparator_Invert);
  D_FF Condition_Flag (.D(xor_1_out), .C(and_5_out), .Q(Condition_Flag_q));  // open: nQ
  and and_5 (and_5_out, clk, Condition_Write);
  and and_6 (Condition_Out, Condition_Flag_q, Condition_Enable);

  // Notes on the sheet:
  //   contents of Control_ROM (hex, n*v repeats v):
  //   c007,0,0,0,0,0,0,0,0,0,0,0,0,0,0,0,c007,0,0,0,0,0,0,0,0,0,0,0,0,0,0,0,c007,0,0,0,
  //   0,0,0,0,0,0,0,0,0,0,0,0,c007,0,0,0,0,0,0,0,0,0,0,0,0,0,0,0,c007,0,0,0,0,0,0,0,0,0,
  //   0,0,0,0,0,0,c007,0,0,0,0,0,0,0,0,0,0,0,0,0,0,0,c007,0,0,0,0,0,0,0,0,0,0,0,0,0,0,0,
  //   c007,0,0,0,0,0,0,0,0,0,0,0,0,0,0,0,c007,0,0,0,0,0,0,0,0,0,0,0,0,0,0,0,c007,0,0,0,
  //   0,0,0,0,0,0,0,0,0,0,0,0,c007,0,0,0,0,0,0,0,0,0,0,0,0,0,0,0,c007,0,0,0,0,0,0,0,0,0,
  //   0,0,0,0,0,0,c007,0,0,0,0,0,0,0,0,0,0,0,0,0,0,0,c007,0,0,0,0,0,0,0,0,0,0,0,0,0,0,0,
  //   c007,0,0,0,0,0,0,0,0,0,0,0,0,0,0,0,c007,0,0,0,0,0,0,0,0,0,0,0,0,0,0,0,c007,0,0,0,
  //   0,0,0,0,0,0,0,0,0,0,0,0,c007,0,0,0,0,0,0,0,0,0,0,0,0,0,0,0,c007,0,0,0,0,0,0,0,0,0,
  //   0,0,0,0,0,0,c007,0,0,0,0,0,0,0,0,0,0,0,0,0,0,0,c007,0,0,0,0,0,0,0,0,0,0,0,0,0,0,0,
  //   c007,0,0,0,0,0,0,0,0,0,0,0,0,0,0,0,c007,0,0,0,0,0,0,0,0,0,0,0,0,0,0,0,c007,0,0,0,
  //   0,0,0,0,0,0,0,0,0,0,0,0,c007,0,0,0,0,0,0,0,0,0,0,0,0,0,0,0,c007,0,0,0,0,0,0,0,0,0,
  //   0,0,0,0,0,0,c007,0,0,0,0,0,0,0,0,0,0,0,0,0,0,0,c007,0,0,0,0,0,0,0,0,0,0,0,0,0,0,0,
  //   c007,0,0,0,0,0,0,0,0,0,0,0,0,0,0,0,c007,0,0,0,0,0,0,0,0,0,0,0,0,0,0,0,c007,0,0,0,
  //   0,0,0,0,0,0,0,0,0,0,0,0,c007,0,0,0,0,0,0,0,0,0,0,0,0,0,0,0,c007,0,0,0,0,0,0,0,0,0,
  //   0,0,0,0,0,0,c007,0,0,0,0,0,0,0,0,0,0,0,0,0,0,0,c007,0,0,0,0,0,0,0,0,0,0,0,0,0,0,0,
  //   c007,0,0,0,0,0,0,0,0,0,0,0,0,0,0,0,c007,0,0,0,0,0,0,0,0,0,0,0,0,0,0,0,c007,0,0,0,
  //   0,0,0,0,0,0,0,0,0,0,0,0,c007,0,0,0,0,0,0,0,0,0,0,0,0,0,0,0,c007,0,0,0,0,0,0,0,0,0,
  //   0,0,0,0,0,0,c007,0,0,0,0,0,0,0,0,0,0,0,0,0,0,0,c007,0,0,0,0,0,0,0,0,0,0,0,0,0,0,0,
  //   c007,0,0,0,0,0,0,0,0,0,0,0,0,0,0,0,c007,0,0,0,0,0,0,0,0,0,0,0,0,0,0,0,c007,0,0,0,
  //   0,0,0,0,0,0,0,0,0,0,0,0,c007,0,0,0,0,0,0,0,0,0,0,0,0,0,0,0,c007,0,0,0,0,0,0,0,0,0,
  //   0,0,0,0,0,0,c007,0,0,0,0,0,0,0,0,0,0,0,0,0,0,0,c007,0,0,0,0,0,0,0,0,0,0,0,0,0,0,0,
  //   c007,0,0,0,0,0,0,0,0,0,0,0,0,0,0,0,c007,0,0,0,0,0,0,0,0,0,0,0,0,0,0,0,c007,0,0,0,
  //   0,0,0,0,0,0,0,0,0,0,0,0,c007,0,0,0,0,0,0,0,0,0,0,0,0,0,0,0,c007,0,0,0,0,0,0,0,0,0,
  //   0,0,0,0,0,0,c007,0,0,0,0,0,0,0,0,0,0,0,0,0,0,0,c007,0,0,0,0,0,0,0,0,0,0,0,0,0,0,0,
  //   c007,0,0,0,0,0,0,0,0,0,0,0,0,0,0,0,c007,0,0,0,0,0,0,0,0,0,0,0,0,0,0,0,c007,0,0,0,
  //   0,0,0,0,0,0,0,0,0,0,0,0,c007,0,0,0,0,0,0,0,0,0,0,0,0,0,0,0,c007,0,0,0,0,0,0,0,0,0,
  //   0,0,0,0,0,0,c007,0,0,0,0,0,0,0,0,0,0,0,0,0,0,0,c007,0,0,0,0,0,0,0,0,0,0,0,0,0,0,0,
  //   c007,0,0,0,0,0,0,0,0,0,0,0,0,0,0,0,c007,0,0,0,0,0,0,0,0,0,0,0,0,0,0,0,c007,0,0,0,
  //   0,0,0,0,0,0,0,0,0,0,0,0,c007,0,0,0,0,0,0,0,0,0,0,0,0,0,0,0,c007,0,0,0,0,0,0,0,0,0,
  //   0,0,0,0,0,0,c007,0,0,0,0,0,0,0,0,0,0,0,0,0,0,0,c007,0,0,0,0,0,0,0,0,0,0,0,0,0,0,0,
  //   c007,0,0,0,0,0,0,0,0,0,0,0,0,0,0,0,c007,0,0,0,0,0,0,0,0,0,0,0,0,0,0,0,c007,0,0,0,
  //   0,0,0,0,0,0,0,0,0,0,0,0,c007,0,0,0,0,0,0,0,0,0,0,0,0,0,0,0,c007,0,0,0,0,0,0,0,0,0,
  //   0,0,0,0,0,0,c007,0,0,0,0,0,0,0,0,0,0,0,0,0,0,0,c007,0,0,0,0,0,0,0,0,0,0,0,0,0,0,0,
  //   c007,0,0,0,0,0,0,0,0,0,0,0,0,0,0,0,c007,0,0,0,0,0,0,0,0,0,0,0,0,0,0,0,c007,0,0,0,
  //   0,0,0,0,0,0,0,0,0,0,0,0,c007,0,0,0,0,0,0,0,0,0,0,0,0,0,0,0,c007,0,0,0,0,0,0,0,0,0,
  //   0,0,0,0,0,0,c007,0,0,0,0,0,0,0,0,0,0,0,0,0,0,0,c007,0,0,0,0,0,0,0,0,0,0,0,0,0,0,0,
  //   c007,0,0,0,0,0,0,0,0,0,0,0,0,0,0,0,c007,0,0,0,0,0,0,0,0,0,0,0,0,0,0,0,c007,0,0,0,
  //   0,0,0,0,0,0,0,0,0,0,0,0,c007,0,0,0,0,0,0,0,0,0,0,0,0,0,0,0,c007,0,0,0,0,0,0,0,0,0,
  //   0,0,0,0,0,0,c007,0,0,0,0,0,0,0,0,0,0,0,0,0,0,0,c007,0,0,0,0,0,0,0,0,0,0,0,0,0,0,0,
  //   c007,0,0,0,0,0,0,0,0,0,0,0,0,0,0,0,c007,0,0,0,0,0,0,0,0,0,0,0,0,0,0,0,c007,0,0,0,
  //   0,0,0,0,0,0,0,0,0,0,0,0,c007,0,0,0,0,0,0,0,0,0,0,0,0,0,0,0,c007,0,0,0,0,0,0,0,0,0,
  //   0,0,0,0,0,0,c007,0,0,0,0,0,0,0,0,0,0,0,0,0,0,0,c007,0,0,0,0,0,0,0,0,0,0,0,0,0,0,0,
  //   c007,0,0,0,0,0,0,0,0,0,0,0,0,0,0,0,c007,0,0,0,0,0,0,0,0,0,0,0,0,0,0,0,c007,0,0,0,
  //   0,0,0,0,0,0,0,0,0,0,0,0,c007,0,0,0,0,0,0,0,0,0,0,0,0,0,0,0,c007,0,0,0,0,0,0,0,0,0,
  //   0,0,0,0,0,0,c007,0,0,0,0,0,0,0,0,0,0,0,0,0,0,0,c007,0,0,0,0,0,0,0,0,0,0,0,0,0,0,0,
  //   c007,0,0,0,0,0,0,0,0,0,0,0,0,0,0,0,c007,0,0,0,0,0,0,0,0,0,0,0,0,0,0,0,c007,0,0,0,
  //   0,0,0,0,0,0,0,0,0,0,0,0,c007,0,0,0,0,0,0,0,0,0,0,0,0,0,0,0,c007,0,0,0,0,0,0,0,0,0,
  //   0,0,0,0,0,0,c007,0,0,0,0,0,0,0,0,0,0,0,0,0,0,0,c007,0,0,0,0,0,0,0,0,0,0,0,0,0,0,0,
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  //   contents of _32kx8_ROM (hex, n*v repeats v):
  //   0,1,2,3,4,5,6,7,8,9,a,b,c,d,e,f
endmodule
